// Logisim project 1bitFullAdder3.circ as structural Verilog: 1 circuit, main circuit main
module main (
  input  A,
  input  B,
  input  Cin,
  output S,
  output Cout
);

  wire and_1_out, and_2_out, and_3_out, and_4_out, xor_1_out;

  ExactlyOne xor_1 (.out(xor_1_out), .in0(A), .in3(B), .in4(Cin));
  and and_1 (and_1_out, A, B, Cin);
  and and_2 (and_2_out, Cin, B);
  and and_3 (and_3_out, Cin, A);
  and and_4 (and_4_out, A, B);
  or or_1 (S, xor_1_out, and_1_out);
  or or_2 (Cout, and_2_out, and_3_out, and_4_out);
endmodule
