// Logisim project 2sCompliment.circ as structural Verilog: 1 circuit, main circuit main
module main (
  input  in_1,
  input  in_2,
  input  in_3,
  input  MINUS,
  input  in_5,
  input  in_6,
  input  in_7,
  input  in_8,
  input  in_9,
  input  in_10,
  input  in_11,
  input  in_12,
  input  in_13,
  input  in_14,
  input  in_15,
  input  in_16,
  input  in_17,
  output out_18,
  output out_19,
  output out_20,
  output out_21,
  output out_22,
  output out_23,
  output out_24,
  output out_25,
  output out_26,
  output out_27
);

  wire adder_1_cout, adder_2_cout, adder_3_cout, and_1_out, and_2_out, and_3_out, and_4_out, not_1_out,
       not_2_out, not_3_out, not_4_out, xor_1_out, xor_2_out, xor_3_out, xor_4_out;

  Adder #(.width(1)) adder_1 (.a(in_1), .b(xor_1_out), .out(out_22), .cin(in_9), .cout(adder_1_cout));
  Adder #(.width(1)) adder_2 (.a(in_2), .b(xor_2_out), .out(out_21), .cin(adder_1_cout), .cout(adder_2_cout));
  Adder #(.width(1)) adder_3 (.a(in_3), .b(xor_3_out), .out(out_20), .cin(adder_2_cout), .cout(adder_3_cout));
  Adder #(.width(1)) adder_4 (.a(MINUS), .b(xor_4_out), .out(out_19), .cin(adder_3_cout), .cout(out_18));
  and and_1 (and_1_out, not_1_out, and_2_out);
  not not_1 (not_1_out, in_5);
  and and_2 (and_2_out, not_2_out, and_3_out);
  xor xor_1 (xor_1_out, not_1_out, and_2_out);
  not not_2 (not_2_out, in_6);
  and and_3 (and_3_out, not_3_out, and_4_out);
  xor xor_2 (xor_2_out, not_2_out, and_3_out);
  not not_3 (not_3_out, in_7);
  xor xor_3 (xor_3_out, not_3_out, and_4_out);
  and and_4 (and_4_out, not_4_out, 1'b1);
  not not_4 (not_4_out, in_8);
  xor xor_4 (xor_4_out, not_4_out, 1'b1);
  _7_Segment_Display u_7_segment_display_1 (
    .g(in_10), .f(in_11), .a(in_12), .b(in_13), .e(in_14), .d(in_15), .c(in_16), .dp(in_17));

  // Notes on the sheet:
  //   LSD
  //   MSD
  //   text here lilol
endmodule
