// Logisim project ALU74181.circ as structural Verilog: 1 circuit, main circuit main
module main (
  input  S3,
  input  S2,
  input  S1,
  input  S0,
  input  in_5,
  input  B3,
  input  A3,
  input  B2,
  input  A2,
  input  B1,
  input  A1,
  input  B0,
  input  A0,
  input  M,
  input  Cn
);

  wire and_1_out, and_2_out, and_3_out, and_4_out, and_5_out, and_6_out, and_7_out, and_8_out, and_9_out,
       and_10_out, and_11_out, and_12_out, and_13_out, and_14_out, and_15_out, and_16_out, and_17_out,
       and_18_out, and_19_out, and_20_out, and_21_out, and_22_out, and_23_out, and_24_out, and_25_out,
       and_26_out, and_27_out, and_28_out, and_29_out, and_30_out, and_31_out, and_32_out, and_33_out,
       and_34_out, and_35_out, and_36_out, and_37_out, and_38_out, and_39_out, nand_1_out, nand_2_out,
       nor_1_out, nor_2_out, nor_9_out, nor_10_out, nor_11_out, nor_12_out, not_1_out, not_2_out, not_3_out,
       not_4_out, not_5_out, not_6_out, not_7_out, not_8_out, not_9_out, not_10_out, not_11_out, or_1_out,
       undriven, undriven_2, xor_1_out, xor_2_out, xor_3_out, xor_4_out;

  not not_1 (not_1_out, B3);
  not not_2 (not_2_out, B2);
  not not_3 (not_3_out, B1);
  not not_4 (not_4_out, B0);
  not not_5 (not_5_out, in_5);
  LED led_1 (.in(not_5_out));
  and and_1 (and_1_out, B3, S3, A3);
  and and_2 (and_2_out, A3, S2, not_1_out);
  and and_3 (and_3_out, not_1_out, S1);
  and and_4 (and_4_out, S0, B3);
  buf and_5 (and_5_out, A3);  // AND_Gate
  and and_6 (and_6_out, B2, S3, A2);
  and and_7 (and_7_out, A2, S2, not_2_out);
  and and_8 (and_8_out, not_2_out, S1);
  and and_9 (and_9_out, S0, B2);
  buf and_10 (and_10_out, A2);  // AND_Gate
  and and_11 (and_11_out, B1, S3, A1);
  and and_12 (and_12_out, A1, S2, not_3_out);
  and and_13 (and_13_out, not_3_out, S1);
  and and_14 (and_14_out, S0, B1);
  buf and_15 (and_15_out, A1);  // AND_Gate
  and and_16 (and_16_out, B0, S3, A0);
  and and_17 (and_17_out, A0, S2, not_4_out);
  and and_18 (and_18_out, not_4_out, S1);
  and and_19 (and_19_out, S0, B0);
  buf and_20 (and_20_out, A0);  // AND_Gate
  LED led_2 (.in(undriven));
  nor nor_1 (nor_1_out, and_1_out, and_2_out);
  LED led_3 (.in(nor_1_out));
  LED led_4 (.in(nor_2_out));
  nor nor_2 (nor_2_out, and_3_out, and_4_out, and_5_out);
  // NOR_Gate nor_3 has open pins: in1=and_6_out, in3=and_7_out, out=open
  // NOR_Gate nor_4 has open pins: in0=and_8_out, in2=and_9_out, in4=and_10_out, out=open
  // NOR_Gate nor_5 has open pins: in1=and_11_out, in3=and_12_out, out=open
  // NOR_Gate nor_6 has open pins: in0=and_13_out, in2=and_14_out, in4=and_15_out, out=open
  // NOR_Gate nor_7 has open pins: in1=and_16_out, in3=and_17_out, out=open
  // NOR_Gate nor_8 has open pins: in0=and_18_out, in2=and_19_out, in4=and_20_out, out=open
  not not_6 (not_6_out, M);
  buf and_21 (and_21_out, nor_2_out);  // AND_Gate
  and and_22 (and_22_out, nor_1_out, undriven_2);
  buf and_23 (and_23_out, nor_1_out);  // AND_Gate
  buf and_24 (and_24_out, nor_1_out);  // AND_Gate
  // AND_Gate and_25 has open pins: out=and_25_out
  // NAND_Gate nand_1 has open pins: out=nand_1_out
  not not_7 (not_7_out, nor_2_out);
  // NOT_Gate not_8 has open pins: in=open, out=not_8_out
  // NOT_Gate not_9 has open pins: in=open, out=not_9_out
  // NOT_Gate not_10 has open pins: in=open, out=not_10_out
  nor nor_9 (nor_9_out, and_21_out, and_22_out, and_23_out, and_24_out);
  // AND_Gate and_26 has open pins: out=and_26_out
  // AND_Gate and_27 has open pins: out=and_27_out
  // AND_Gate and_28 has open pins: out=and_28_out
  // AND_Gate and_29 has open pins: out=and_29_out
  // AND_Gate and_30 has open pins: out=and_30_out
  // AND_Gate and_31 has open pins: out=and_31_out
  // AND_Gate and_32 has open pins: out=and_32_out
  // AND_Gate and_33 has open pins: out=and_33_out
  // AND_Gate and_34 has open pins: out=and_34_out
  nand nand_2 (nand_2_out, not_6_out, not_6_out, Cn);
  and and_35 (and_35_out, undriven_2, not_7_out);
  nor nor_10 (nor_10_out, and_26_out, and_27_out, and_28_out, and_29_out);
  buf and_36 (and_36_out, not_8_out);  // AND_Gate
  nor nor_11 (nor_11_out, and_30_out, and_31_out, and_32_out);
  buf and_37 (and_37_out, not_9_out);  // AND_Gate
  nor nor_12 (nor_12_out, and_33_out, and_34_out);
  buf and_38 (and_38_out, not_10_out);  // AND_Gate
  not not_11 (not_11_out, nor_9_out);
  or or_1 (or_1_out, not_11_out, and_25_out);
  xor xor_1 (xor_1_out, and_35_out, nor_10_out);
  xor xor_2 (xor_2_out, and_36_out, nor_11_out);
  xor xor_3 (xor_3_out, and_37_out, nor_12_out);
  xor xor_4 (xor_4_out, and_38_out, nand_2_out);
  and and_39 (and_39_out, xor_2_out, xor_1_out, xor_3_out, xor_4_out);
  LED led_5 (.in(nor_9_out));
  LED led_6 (.in(or_1_out));
  LED led_7 (.in(nand_1_out));
  LED led_8 (.in(xor_1_out));
  LED led_9 (.in(xor_2_out));
  LED led_10 (.in(and_39_out));
  LED led_11 (.in(xor_3_out));
  LED led_12 (.in(xor_4_out));

  // Notes on the sheet:
  //   why is there a random ahhh and gate here
  //   all technically notted but idrgaf
  //   G
  //   Cn + 4
  //   P
  //   F3
  //   F2
  //   A = B
  //   F1
  //   F0
endmodule
