// Logisim project displayFucking.circ as structural Verilog: 1 circuit, main circuit main
module main (
  input  in_1,
  input  in_2,
  input  in_3,
  input  in_4,
  input  in_5,
  input  in_6,
  input  in_7,
  input  in_8,
  input  in_9,
  input  in_10,
  input  in_11,
  input  in_12,
  input  in_13,
  input  in_14,
  input  in_15,
  input  in_16
);

  _7_Segment_Display u_7_segment_display_1 (
    .g(in_9), .f(in_10), .a(in_11), .b(in_12), .e(in_13), .d(in_14), .c(in_15), .dp(in_16));
  _7_Segment_Display u_7_segment_display_2 (
    .g(in_1), .f(in_2), .a(in_3), .b(in_4), .e(in_5), .d(in_6), .c(in_7), .dp(in_8));
endmodule
