// Logisim project simplifiedAdder2.circ as structural Verilog: 1 circuit, main circuit main
module main (
  input  in_1,
  input  in_2,
  input  in_3,
  input  PLUS,
  input  in_5,
  input  in_6,
  input  in_7,
  input  in_8,
  input  in_9,
  input  in_10,
  input  in_11,
  input  in_12,
  input  in_13,
  input  in_14,
  input  in_15,
  input  in_16,
  input  in_17,
  output out_18,
  output out_19,
  output out_20,
  output out_21,
  output out_22
);

  wire adder_1_cout, adder_2_cout, adder_3_cout;

  Adder #(.width(1)) adder_1 (.a(in_1), .b(in_5), .out(out_22), .cin(in_9), .cout(adder_1_cout));
  Adder #(.width(1)) adder_2 (.a(in_2), .b(in_6), .out(out_21), .cin(adder_1_cout), .cout(adder_2_cout));
  Adder #(.width(1)) adder_3 (.a(in_3), .b(in_7), .out(out_20), .cin(adder_2_cout), .cout(adder_3_cout));
  Adder #(.width(1)) adder_4 (.a(PLUS), .b(in_8), .out(out_19), .cin(adder_3_cout), .cout(out_18));
  _7_Segment_Display u_7_segment_display_1 (
    .g(in_10), .f(in_11), .a(in_12), .b(in_13), .e(in_14), .d(in_15), .c(in_16), .dp(in_17));

  // Notes on the sheet:
  //   LSD
  //   MSD
  //   text here lilol
endmodule
